# Fritzing sketch schematic (saved by Fritzing 0.9.3b)
breadboards: 1

parts:
  LED1 = smd LED [color="Red (633nm)" package="0603 [SMD]"]
  LED2 = smd LED [color="Green (565nm)" package="0603 [SMD]"]
  LED3 = smd LED [color="Yellow (595nm)" package="0603 [SMD]"]
  R1 = Resistor [tolerance=±5% resistance=220 package="1206 [SMD]"]
  R2 = Resistor [tolerance=±5% resistance=220 package="1206 [SMD]"]
  R3 = Resistor [tolerance=±5% resistance=220 package="1206 [SMD]"]
  ESP32_-_Back1 = ESP32 - CAM
  S1 = Momentary Switch [package=ksa_sealed_tac_switch]

nets:
  N1: LED1.cathode, LED2.cathode, LED3.cathode, ESP32_-_Back1.GND
  N2: LED1.anode, R3.Pin_0
  N3: LED2.anode, R2.Pin_0
  N4: LED3.anode, R1.Pin_0
  N5: R1.Pin_1, ESP32_-_Back1.GPIO14
  N6: R2.Pin_1, ESP32_-_Back1.GPIO15
  N7: R3.Pin_1, ESP32_-_Back1.GPIO13
  N8: ESP32_-_Back1.GPIO12, S1.3
  N9: ESP32_-_Back1.3.3V, S1.4

custom parts:
  ESP32 - CAM: The ESP32-CAM has a very competitive small-size camera module that can operate independently as a minimum system with a footprint of only 27*40.5*4.5mm and a deep sleep current of up to 6mA.
